# Fritzing sketch 01_Tilt_Switch (saved by Fritzing 0.9.3b)
breadboards: 1

parts:
  Part1 = Itsy Bitsy 32u4 5V @ 16MHz [part_number="Adafruit #3677"]
  S1 = Tilt Switch [package=THT]

nets:
  N1: Part1.GND, S1.Pin_2
  N2: Part1.D5, S1.Pin_1

custom parts:
  Itsy Bitsy 32u4 5V @ 16MHz: What's smaller than a Feather but larger than a Trinket? It's an Itsy Bitsy! Small, powerful, Arduino-compatible - this microcontroller board is perfect when you want something very compact, but still with a bunch of pins. Itsy Bitsy is only 1.4" long by 0.7" wide, but has 6 power pins, 6 analog & digital pins and 17 digital pins. It packs much of the same capability as an Arduino UNO. So it's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
